# Fritzing sketch wiring (saved by Fritzing 0.9.3b)
breadboards: 1

parts:
  Raspberry_Pi_1 = Raspberry Pi 3 [part_number=RPI-3-V1.2]
  LCD1 = LCD screen
  R1 = Resistor [tolerance=±5% resistance=220 package="0603 [SMD]"]
  R2 = Resistor [tolerance=±5% resistance=220 package="0603 [SMD]"]
  R3 = Trimmer Potentiometer [maximum_resistance=10kΩ package=THT]
  LED3 = smd LED [color="Red (633nm)" package="0603 [SMD]"]
  LED4 = smd LED [color="Red (633nm)" package="0603 [SMD]"]
  J2 = Basic Servo

nets:
  N1: Raspberry_Pi_1.GPIO27, LED4.cathode
  N2: Raspberry_Pi_1.GPIO22, Raspberry_Pi_1.3V3, J2.pulse
  N3: Raspberry_Pi_1.GPIO5, LED3.cathode
  N4: Raspberry_Pi_1.GPIO6, LCD1.DB6
  N5: Raspberry_Pi_1.GPIO13, LCD1.DB7
  N6: Raspberry_Pi_1.GPIO19, Raspberry_Pi_1.GPIO26, LCD1.DB5
  GND: Raspberry_Pi_1.GND, Raspberry_Pi_1.GPIO12, Raspberry_Pi_1.GPIO24, Raspberry_Pi_1.GPIO14, LCD1.VSS, LCD1.E, LCD1.DB4, LCD1.LED-, R1.Pin_0, R2.Pin_1, R3.leg2, J2.gnd
  N7: Raspberry_Pi_1.GPIO23, LCD1.RS
  5V: Raspberry_Pi_1.5V, LCD1.VDD, LCD1.LED+, R3.leg1, J2.vcc
  N8: LCD1.V0, R3.wiper
  N9: R1.Pin_1, LED3.anode
  N10: R2.Pin_0, LED4.anode
